# Fritzing sketch PowerStrip (saved by Fritzing 0.9.3b)

parts:
  Raspberry_Pi_Zero1 = Raspberry Pi Zero
  U1 = 4-Channel 5v Relay Shield [package=relay-4ch5v10a]

nets:
  N1: Raspberry_Pi_Zero1.GPIO17, U1.IN4
  N2: Raspberry_Pi_Zero1.GPIO27, U1.IN3
  N3: Raspberry_Pi_Zero1.GPIO22, U1.IN2
  N4: Raspberry_Pi_Zero1.GPIO11, U1.GND
  N5: Raspberry_Pi_Zero1.GPIO24, U1.IN1
  5V: Raspberry_Pi_Zero1.5V, U1.VCC
  N6: U1.K2-In, U1.K2-On, U1.K4-On

custom parts:
  4-Channel 5v Relay Shield: 4 Channel 5v Relay Shield w. 2x SPD-06VDC-SD-C
