# Fritzing sketch lighting (saved by Fritzing 0.9.3b)
breadboards: 1

parts:
  Part2 = 16-Channel 12-bit PWM Servo Driver - I2C [part_number=815]
  Raspberry_Pi_Zero1 = Raspberry Pi Zero
  Q1 = NPN-Transistor [part_number=PN2222A package="TO92 [THT]"]
  Q2 = NPN-Transistor [part_number=PN2222A package="TO92 [THT]"]
  R1 = Resistor [tolerance=±5% resistance=10k package=THT]
  R2 = Resistor [tolerance=±5% resistance=1k package=THT]
  R3 = Resistor [tolerance=±5% resistance=10k package=THT]
  R4 = Resistor [tolerance=±5% resistance=1k package=THT]
  Power_plug1 = Power plug [part_number="12 volt dc"]
  U1 = 3.5mm Audio Jack [package=audio-jack-3.5mm-smd]

nets (from the breadboard view):
  N1: Part2.PWM1, R3.Pin_0
  GND: Part2.GND, Raspberry_Pi_Zero1.GND, Q1.E, Q2.E, Power_plug1.GND, U1.SLEEVE
  N2: Part2.PWM0, R1.Pin_0
  VCC: Part2.VCC, Raspberry_Pi_Zero1.5V
  N3: Part2.SDA, Raspberry_Pi_Zero1.GPIO2
  N4: Part2.SCL, Raspberry_Pi_Zero1.GPIO3
  N5: Q1.B, R3.Pin_1
  N6: Q1.C, R2.Pin_0, U1.RIGHT
  N7: Q2.B, R1.Pin_1
  N8: Q2.C, R4.Pin_0, U1.LEFT
  N9: R2.Pin_1, R4.Pin_1, Power_plug1.VCC

custom parts:
  16-Channel 12-bit PWM Servo Driver - I2C: You want to make a cool robot, maybe a hexapod walker, or maybe just a piece of art with a lot of moving parts. Or maybe you want to drive a lot of LEDs with precise PWM output. Using only two pins, control 16 free-running PWM outputs! You can even chain up 62 breakouts to control up to 992 PWM outputs.
