# Fritzing sketch temperature (saved by Fritzing 0.9.3b)
breadboards: 1

parts:
  Raspberry_Pi_Zero2 = Raspberry Pi Zero
  U2 = 4-Channel 5v Relay Shield [package=relay-4ch5v10a]
  DS1 = DS18B20 1-Wire Temperature Sensor [part_number=DS18B20]
  R1 = Resistor [tolerance=±5% resistance=220 package=THT]

nets:
  3V3: Raspberry_Pi_Zero2.3v3, Raspberry_Pi_Zero2.3V3, DS1.VDD, R1.Pin_0
  N1: Raspberry_Pi_Zero2.GPIO4, DS1.DQ, R1.Pin_1
  GND: Raspberry_Pi_Zero2.GND, U2.GND, DS1.GND
  5V: Raspberry_Pi_Zero2.5V, U2.VCC

custom parts:
  4-Channel 5v Relay Shield: 4 Channel 5v Relay Shield w. 2x SPD-06VDC-SD-C
